# Fritzing sketch CENG317_PCB_DESIGN (saved by Fritzing 0.9.3b)
circuit board: 8.46667cm x 5.64444cm
breadboards: 1

parts:
  hc-sr1 = hc-sr04
  Part1 = Arduino Uno (Rev3) - ICSP
  DHT1 = Humidity and Temperature Sensor DHT11

nets:
  VCC: hc-sr1.VCC, Part1.5V, DHT1.Vcc
  N1: hc-sr1.Trig, Part1.ICSP_MOSI, Part1.D11_PWM/MOSI
  N2: hc-sr1.Echo, Part1.D12/MISO
  GND: hc-sr1.GND, Part1.GND, DHT1.GND_1
  N3: Part1.A0, DHT1.Data-signal

custom parts:
  Humidity and Temperature Sensor DHT11: Digital relative humidity & temperature sensor DHT11
